# Fritzing sketch Gas sensor app (saved by Fritzing 0.9.4)
breadboards: 1

parts:
  Mod1 = Raspberry Pi Pico W
  R1 = Resistor [tolerance=±5% resistance=220 package=THT]
  R2 = Resistor [tolerance=±5% resistance=220 package=THT]
  R3 = Resistor [tolerance=±5% resistance=220 package=THT]
  LED1 = RGB LED (com. cathode, rgb) [package="5 mm [THT]"]
  J1 = Piezo Speaker
  Parça1 = MQ-4

nets:
  N1: Mod1.pin_3, Mod1.pin_8, Mod1.pin_13, Mod1.pin_18, Mod1.pin_23, Mod1.pin_28, Mod1.pin_33, Mod1.pin_38, Mod1.pin_42, R1.Pin_1, R2.Pin_1, R3.Pin_0, J1.pin1
  N2: Mod1.pin_12, J1.pin2
  N3: Mod1.pin_14, LED1.red_anode
  N4: Mod1.pin_15, LED1.green_anode
  N5: Mod1.pin_16, LED1.blue_anode
  N6: Mod1.pin_31, Parça1.AO
  N7: Mod1.pin_36, Parça1.VCC
  N8: R2.Pin_0, LED1.common_cathode
  N9: R3.Pin_1, Parça1.GND

custom parts:
  Raspberry Pi Pico W: Raspberry Pi Pico W. Based around the RP2040 microcontroller the Pico W is a low cost microcontroller device bringing Raspberry Pi quality, cost, and easy of use to the microcontroller space. The areas marked KEEPOUT in pcb silkscreen should not have traces running through them to avoid shorts on a soldered in module!
